# Fritzing sketch Untitled Sketch (saved by Fritzing 0.9.6b)
breadboards: 1

parts:
  Part1 = Arduino Uno (Rev3)
  S1 = Pushbutton [package="[THT]"]
  S2 = Pushbutton [package="[THT]"]
  S3 = Pushbutton [package="[THT]"]
  R1 = Resistor [tolerance=±5% power=0.25 resistance=10k package=THT]
  R2 = Resistor [tolerance=±5% power=0.25 resistance=10k package=THT]
  R3 = Resistor [tolerance=±5% power=0.25 resistance=10k package=THT]
  LCD1 = LCD screen
  R4 = Rotary Potentiometer (Small) [maximum_resistance=100kΩ package=THT]
  R5 = Resistor [tolerance=±5% power=0.25 resistance=220 package=THT]

nets:
  N1: Part1.D8, S1.Pin_1, S1.Pin_2, R3.Pin_0
  N2: Part1.D11_PWM/MOSI, LCD1.E
  N3: Part1.D12/MISO, LCD1.RS
  N4: Part1.D2, LCD1.DB4
  N5: Part1.D3_PWM, LCD1.DB5
  N6: Part1.D4, LCD1.DB6
  N7: Part1.D5_PWM, LCD1.DB7
  N8: Part1.D6_PWM, S3.Pin_1, S3.Pin_2, R2.Pin_0
  N9: Part1.D7, S2.Pin_1, S2.Pin_2, R1.Pin_0
  5V: Part1.5V, S1.Pin_3, S1.Pin_4, S2.Pin_3, S2.Pin_4, S3.Pin_3, S3.Pin_4, LCD1.VDD, R4.leg1, R5.Pin_1
  GND: Part1.GND, R1.Pin_1, R2.Pin_1, R3.Pin_1, LCD1.VSS, LCD1.R/W, LCD1.LED-, R4.leg2
  N10: LCD1.V0, R4.wiper
  N11: LCD1.LED+, R5.Pin_0

// code stored in the sketch: cableMeasure.ino
/* 
Arduino device to automatically measure cable length pulled. 
Bill Addison
26 February 2021
*/


#include <LiquidCrystal.h>
#include <EEPROM.h>
#include <Arduino.h>

LiquidCrystal lcd (12, 11, 2, 3, 4, 5);

//constants to define which pins or the arduino are used for what.
const int encPin1 = 9; //rotary encoder attached to measuring wheel CLK
const int encPin2 = 10; //rotary encoder attached to measuring wheel DATA
const int switchPin1 = 6; //Switch 1 - decrease the target length
const int switchPin2 = 7; //Switch 2 - increase the target length
const int switchPin3 = 8; //Switch 3 - reset the measured length to 0
const int targetLengthIndicator = 13; //output pin used to indicate the measured length is a multiple of the target length


// variables to analyse the rotary encoder position
int pos = 0; //this will increment (or decrement) by 1 for each clockwise (counterclockwise) "click" of the rotary encoder
int state;
int lastState;

// variables to store measured and target length
int targetLength;
int measuredLength = 0;

//variable to analyse and debounce the three switch inputs
int switchState1;
int switchState2;
int switchState3;
int lastSwitchState1 = LOW;
int lastSwitchState2 = LOW;
int lastSwitchState3 = LOW;
unsigned long lastDebounceTime1 = 0;  
unsigned long lastDebounceTime2 = 0;  
unsigned long lastDebounceTime3 = 0;  
unsigned long debounceDelay = 50;

//constants used to convert 'pos' variable into a length
const int C = 1; //circumference of measuring wheel
const int N = 1; //number of "clicks" for one revolution of wheel


void setup(){
    //define pinModes
    pinMode (encPin1 ,INPUT);
    pinMode (encPin2 ,INPUT);
    pinMode (switchPin1 ,INPUT);
    pinMode (switchPin2 ,INPUT);
    pinMode (switchPin3 ,INPUT);
    pinMode (targetLengthIndicator, OUTPUT);

    //read initial values required.
    lastState = digitalRead(encPin1); 
    digitalWrite(targetLengthIndicator, LOW);
    targetLength =  EEPROM.read(0);

    //initilise LCD display
    lcd.begin(16, 2);
    lcd.print("Cable Measure");
    // lcd.setCursor(0,1);
    // lcd.print("V0 210225");
    Serial.begin(9600);
}

// main loop

void loop(){

    //read rotary encoder and increment or decrement  position accordingly
    state = digitalRead(encPin1);
    if (state != lastState){     
        if (digitalRead(encPin2) != state) { 
            pos ++;
        } 
        else {
            pos --;
        }
    } 
    lastState = state;

    //calculate measured length

    measuredLength = pos*C/N;

    //read from switch 1 and action

    int s1 = digitalRead(switchPin1);
    if (s1 != lastSwitchState1){
        lastDebounceTime1 = millis();
    }
    if ((millis() - lastDebounceTime1) > debounceDelay) {
        if (s1 != switchState1) {
            switchState1 = s1;
            if(switchState1 == HIGH && targetLength > 0){
                targetLength--;
                EEPROM.update(0,targetLength);
            }
        }
    } 
    lastSwitchState1 = s1;

    //read from switch 2 and action

    int s2 = digitalRead(switchPin2);
    if (s2 != lastSwitchState2){
        lastDebounceTime2 = millis();
    }
    if ((millis() - lastDebounceTime2) > debounceDelay) {
        if (s2 != switchState2) {
            switchState2 = s2;
            if(switchState2 == HIGH){
                targetLength++;
                EEPROM.update(0,targetLength);
            }
        }
    } 
    lastSwitchState2 = s2;

    //read from switch 3 action
    
    int s3 = digitalRead(switchPin3);
    if (s3 != lastSwitchState3){
        lastDebounceTime3 = millis();
    }
    if ((millis() - lastDebounceTime3) > debounceDelay) {
        if (s3 != switchState3) {
            switchState3 = s3;
            if(switchState3 == HIGH){
                pos = 0;
            }
        }
    } 
    lastSwitchState3 = s3;

    //check if target length met

    if (targetLength > 0 and measuredLength%targetLength ==0)
    {
        digitalWrite(targetLengthIndicator, HIGH);
    }
    else{
        digitalWrite(targetLengthIndicator, LOW);
    }
    

    //print results to LCD

    lcd.setCursor(0, 1);
    char buff[8];
    sprintf(buff, "%4d", measuredLength);
    lcd.print(buff);
    lcd.setCursor(9, 1);
    char buff2[8];
    sprintf(buff2, "%4d", targetLength);
    lcd.print(buff2);

    //serial comms for testing

    Serial.print(s1);
    Serial.print("\t");
    Serial.print(measuredLength);
    Serial.print("\t");
    Serial.print(targetLength);
    Serial.println();

  

    
 

}
